# Fritzing sketch flood-pi (saved by Fritzing 0.8.7b)
breadboards: 1

parts:
  Raspberry_Pi_B_rev1 = Raspberry Pi B rev1
  IC1 = MCP3008 8-channel 10-bit ADC [part_number=MCP3008]
  LED1 = LED - 5mm [color="Red (633nm)" package="5 mm [THT]"]
  R1 = Resistor [tolerance=±5% resistance=220 package=THT]

nets:
  N1: Raspberry_Pi_B_rev1.5V, IC1.no_name_yet#15, IC1.no_name_yet#16
  N2: Raspberry_Pi_B_rev1.GND, Raspberry_Pi_B_rev1.GPIO_14, IC1.no_name_yet#9, IC1.no_name_yet#14, LED1.cathode
  N3: Raspberry_Pi_B_rev1.GPIO_10, IC1.no_name_yet#11
  N4: Raspberry_Pi_B_rev1.GPIO_9, IC1.no_name_yet#12
  N5: Raspberry_Pi_B_rev1.GPIO_25, Raspberry_Pi_B_rev1.GPIO_8, IC1.no_name_yet#10
  N6: Raspberry_Pi_B_rev1.GPIO_11, IC1.no_name_yet#13
  N7: IC1.no_name_yet#1, LED1.anode, R1.Pin_0
